// Logisim project 2 Bit ALU.circ as structural Verilog: 3 circuits, main circuit main
module main (
  input  [1:0] Operand_A,
  input  [1:0] Operand_B,
  input  Sub,
  input  [2:0] ALU_Op,
  input  in_5,
  output [1:0] Result,
  output Carry_Borrow,
  output A_B,
  output A_B_2,
  output A_B_3,
  output [3:0] Multiply
);

  wire ALU0_carry_borrow;

  Comparator #(.width(2)) comparator_1 (.a(Operand_A), .b(Operand_B), .gt(A_B), .eq(A_B_2), .lt(A_B_3));
  _1_Bit_ALU ALU0 (
    .Carry_In(Sub), .Sub(Sub), .Operand_B(Operand_B[0]), .Operand_A(Operand_A[0]),
    .Carry_Borrow(ALU0_carry_borrow), .ALU_Op(ALU_Op), .Result(Result[0]));
  _1_Bit_ALU ALU1 (
    .Carry_In(ALU0_carry_borrow), .Sub(Sub), .Operand_B(Operand_B[1]), .Operand_A(Operand_A[1]),
    .Carry_Borrow(Carry_Borrow), .ALU_Op(ALU_Op), .Result(Result[1]));
  Multi multi_1 (
    .A0(Operand_A[0]), .A1(Operand_A[1]), .B0(Operand_B[0]), .B1(Operand_B[1]), .in_5(in_5),
    .R0(Multiply[0]), .R1(Multiply[1]), .R2(Multiply[2]), .R4(Multiply[3]));
endmodule

module _1_Bit_ALU (
  input  Operand_B,
  input  Operand_A,
  input  Carry_In,
  input  Sub,
  input  [2:0] ALU_Op,
  output Result,
  output Carry_Borrow
);

  wire adder_1_out, and_1_out, multiplexer_1_out, not_1_out, not_2_out, or_1_out, xor_1_out;

  not not_1 (not_1_out, Operand_B);
  Multiplexer multiplexer_1 (.in0(Operand_B), .in1(not_1_out), .out(multiplexer_1_out), .sel(Sub));  // open: en
  not not_2 (not_2_out, Operand_A);
  and and_1 (and_1_out, Operand_A, Operand_B);
  or or_1 (or_1_out, Operand_A, Operand_B);
  xor xor_1 (xor_1_out, Operand_A, Operand_B);
  Adder #(.width(1)) adder_1 (
    .a(Operand_A), .b(multiplexer_1_out), .out(adder_1_out), .cin(Carry_In), .cout(Carry_Borrow));
  Multiplexer #(.select(3)) multiplexer_2 (
    .in0(not_2_out), .in1(and_1_out), .in2(or_1_out), .in3(xor_1_out), .in4(adder_1_out), .out(Result),
    .sel(ALU_Op));  // open: in5, in6, in7, en
endmodule

module Multi (
  input  A0,
  input  A1,
  input  B0,
  input  B1,
  input  in_5,
  output R0,
  output R1,
  output R2,
  output R4
);

  wire adder_1_cout, and_2_out, and_3_out, and_4_out;

  and and_1 (R0, A0, B0);
  and and_2 (and_2_out, A0, B1);
  and and_3 (and_3_out, A1, B0);
  and and_4 (and_4_out, A1, B1);
  Adder #(.width(1)) adder_1 (.a(and_2_out), .b(and_3_out), .out(R1), .cout(adder_1_cout));  // open: cin
  Adder #(.width(1)) adder_2 (.a(and_4_out), .b(in_5), .out(R2), .cin(adder_1_cout), .cout(R4));
endmodule
